// Logisim project DataPath.circ as structural Verilog: 3 circuits, main circuit main
module main (
);

  RF rf_1 ();  // open: ReadReg_1, ReadReg_2, Write, Write_data, ReadData_1, ReadData_2
endmodule

module ALU (
  input  [3:0] reg1,
  input  [3:0] reg2,
  input  [1:0] opcode,
  output [3:0] ALUout
);

  wire [3:0] adder_1_out, divider_1_out, multiplier_1_out, subtractor_1_out;

  Adder #(.width(4)) adder_1 (.a(reg1), .b(reg2), .out(adder_1_out));  // open: cin, cout
  Subtractor #(.width(4)) subtractor_1 (.a(reg1), .b(reg2), .out(subtractor_1_out));  // open: bin, bout
  Multiplier #(.width(4)) multiplier_1 (.a(reg1), .b(reg2), .out(multiplier_1_out));  // open: cin, cout
  Divider #(.width(4)) divider_1 (.a(reg1), .b(reg2), .out(divider_1_out));  // open: upper, rem
  Multiplexer #(.select(2), .width(4)) multiplexer_1 (
    .in0(adder_1_out), .in1(subtractor_1_out), .in2(multiplier_1_out), .in3(divider_1_out), .out(ALUout),
    .sel(opcode));
endmodule

module RF (
  input  [1:0] ReadReg_1,
  input  [1:0] ReadReg_2,
  input  Write,
  input  [3:0] Write_data,
  output [3:0] ReadData_1,
  output [3:0] ReadData_2
);

  wire and_1_out, and_2_out, and_3_out, and_4_out, decoder_1_out0, decoder_1_out1, decoder_1_out2,
       decoder_1_out3;
  wire [3:0] register_1_q, register_2_q, register_3_q;

  and and_1 (and_1_out, Write, decoder_1_out0);
  and and_2 (and_2_out, Write, decoder_1_out1);
  and and_3 (and_3_out, Write, decoder_1_out2);
  and and_4 (and_4_out, Write, decoder_1_out3);
  Register #(.width(4)) register_1 (.D(Write_data), .Q(register_1_q), .clr(and_1_out));  // open: en, clk
  Register #(.width(4)) register_2 (.D(Write_data), .Q(register_2_q), .clr(and_2_out));  // open: en, clk
  Register #(.width(4)) register_3 (.D(Write_data), .Q(register_3_q), .clr(and_3_out));  // open: en, clk
  Register #(.width(4)) register_4 (.D(Write_data), .Q(register_3_q), .clr(and_4_out));  // open: en, clk
  Decoder #(.select(2)) decoder_1 (
    .out0(decoder_1_out0), .out1(decoder_1_out1), .out2(decoder_1_out2), .out3(decoder_1_out3));  // open: sel, en
  Multiplexer #(.select(2), .width(4)) multiplexer_1 (
    .in0(register_1_q), .in1(register_2_q), .in2(register_3_q), .in3(register_3_q), .out(ReadData_1),
    .sel(ReadReg_1));
  Multiplexer #(.select(2), .width(4)) multiplexer_2 (
    .in0(register_1_q), .in1(register_2_q), .in2(register_3_q), .in3(register_3_q), .out(ReadData_2),
    .sel(ReadReg_2));
endmodule
